# Fritzing sketch Temperature (saved by Fritzing 0.9.2b)
breadboards: 1

parts:
  T1 = TMP36 Temperature Sensor [package="TO92 [THT]"]
  IC1 = MCP3008 8-channel 10-bit ADC [part_number=MCP3008]
  J3 = T Cobbler Plus

nets:
  N1: T1.+Vs, IC1.no_name_yet#15, IC1.no_name_yet#16, J3.3V3
  N2: T1.Vout, IC1.no_name_yet#1
  N3: T1.GND, IC1.no_name_yet#9, IC1.no_name_yet#14, J3.SCLK
  N4: IC1.no_name_yet#10, J3.#6
  N5: IC1.no_name_yet#11, J3.#5
  N6: IC1.no_name_yet#12, J3.EEC
  N7: IC1.no_name_yet#13, J3.CE1

custom parts:
  T Cobbler Plus: The T-Cobbler Plus is an add on prototyping board from Adafruit specifically designed for the Raspberry Pi B+ that can break out all those tasty power, GPIO, I2C and SPI pins from the 40-pin header onto a solderless breadboard. This set will make "cobbling together" prototypes with the Pi super easy. The T-Cobbler Plus can plug into any solderless breadboard.
